// Digital circuit Solitaire_1b.dig as structural Verilog
module Solitaire_1b (
  input  x,
  input  y,
  input  z,
  output F
);

  wire and_1_out, and_2_out, and_3_out, and_4_out, and_5_out, and_6_out, not_1_out, not_2_out, or_1_out;

  not not_1 (not_1_out, y);
  not not_2 (not_2_out, x);
  and and_1 (and_1_out, x, y);
  and and_2 (and_2_out, x, not_1_out);
  and and_3 (and_3_out, and_1_out, z);
  and and_4 (and_4_out, not_1_out, not_2_out);
  and and_5 (and_5_out, and_2_out, z);
  and and_6 (and_6_out, z, and_4_out);
  or or_1 (or_1_out, and_3_out, and_5_out);
  or or_2 (F, or_1_out, and_6_out);

  // Notes on the sheet:
  //   XY^
  //   XYZ
endmodule
