// Digital circuit Solitaire_1e.dig as structural Verilog
module Solitaire_1e (
  input  X,
  input  y,
  input  Z,
  output F
);

  wire and_1_out, and_2_out;

  and and_1 (and_1_out, X, y);
  and and_2 (and_2_out, and_1_out, Z);
  or or_1 (F, and_2_out, Z);
endmodule
