// Digital circuit Solitaire_2d.dig as structural Verilog
module Solitaire_2d (
  input  A,
  input  B,
  input  C,
  output Q
);

  wire and_1_out, not_1_out, not_2_out, not_3_out;

  not not_1 (not_1_out, A);
  not not_2 (not_2_out, B);
  not not_3 (not_3_out, C);
  and and_1 (and_1_out, not_2_out, not_3_out);
  or or_1 (Q, not_1_out, and_1_out);
endmodule
