// Digital circuit Solitaire_3a.dig as structural Verilog
module Solitaire_3a (
  input  X,
  input  Y,
  input  Z,
  output F
);

  wire not_1_out, not_2_out;

  not not_1 (not_1_out, Z);
  not not_2 (not_2_out, Z);
  or or_1 (F, not_1_out, Y, not_2_out);
endmodule
