// Digital circuit Solitaire_3b.dig as structural Verilog
module Solitaire_3b (
  input  A,
  input  B,
  input  C,
  input  D,
  output F
);

  wire and_1_out, and_2_out, and_3_out, and_4_out, not_1_out, not_2_out;

  and and_1 (and_1_out, A, B);
  not not_1 (not_1_out, C);
  not not_2 (not_2_out, B);
  and and_2 (and_2_out, and_1_out, C);
  and and_3 (and_3_out, not_1_out, not_2_out);
  and and_4 (and_4_out, and_2_out, D);
  or or_1 (F, and_3_out, and_4_out);
endmodule
