// Digital circuit Solitaire_4s.dig as structural Verilog
module Solitaire_4s (
  input  W,
  input  X,
  input  Y,
  input  Z,
  output F
);

  wire and_1_out, and_2_out, and_3_out, and_4_out, and_5_out, not_1_out, not_2_out, not_3_out, or_1_out;

  and and_1 (and_1_out, X, Y);
  not not_1 (not_1_out, X);
  not not_2 (not_2_out, W);
  and and_2 (and_2_out, not_1_out, not_2_out);
  and and_3 (and_3_out, not_2_out, and_1_out);
  not not_3 (not_3_out, Z);
  and and_4 (and_4_out, not_1_out, not_3_out);
  and and_5 (and_5_out, W, and_4_out);
  or or_1 (or_1_out, and_2_out, and_3_out);
  or or_2 (F, or_1_out, and_5_out);
endmodule
