// Digital circuit lab03_2.dig as structural Verilog
module lab03_2 (
  input  A,
  input  B,
  input  C,
  output f
);

  wire and_1_out, nand_1_out, nor_1_out, not_1_out;

  not not_1 (not_1_out, B);
  and and_1 (and_1_out, B, C);
  nand nand_1 (nand_1_out, A, not_1_out);
  nor nor_1 (nor_1_out, A, and_1_out);
  nor nor_2 (f, nand_1_out, nor_1_out);

  // Notes on the sheet:
  //   A: A
endmodule
