// Digital circuit 2c-improved.dig as structural Verilog
module _2c_improved (
  input  X,
  input  clk,
  output A,
  output B,
  output C
);

  wire and_1_out, and_2_out, and_3_out, DA_nq, DC_nq, not_1_out, or_1_out, or_2_out;

  not not_1 (not_1_out, X);
  D_FF DB (.D(or_1_out), .C(clk), .Q(A));  // open: nQ
  D_FF DA (.D(or_2_out), .C(clk), .Q(B), .nQ(DA_nq));
  D_FF DC (.D(X), .C(clk), .Q(C), .nQ(DC_nq));
  and and_1 (and_1_out, not_1_out, DA_nq, A);
  and and_2 (and_2_out, B, DC_nq);
  and and_3 (and_3_out, DA_nq, C);
  or or_1 (or_1_out, and_1_out, DC_nq);
  or or_2 (or_2_out, and_2_out, and_3_out);
endmodule
