// Digital circuit Solitaire_1b.dig as structural Verilog
module Solitaire_1b (
  input  X0,
  input  X1,
  input  X2,
  input  X3,
  output B,
  output C,
  output A
);

  wire and_1_out, and_2_out, and_3_out, and_4_out, and_5_out, nand_2_out, nand_3_out, not_1_out, not_2_out,
       or_2_out;

  not not_1 (not_1_out, X0);
  nand nand_1 (C, X1, X0);
  and and_1 (and_1_out, X1, not_1_out);
  not not_2 (not_2_out, X1);
  or or_1 (A, C, and_1_out);
  and and_2 (and_2_out, X2, not_2_out);
  nand nand_2 (nand_2_out, X3, X2);
  and and_3 (and_3_out, and_2_out, X0);
  and and_4 (and_4_out, nand_2_out, X1);
  nand nand_3 (nand_3_out, X0, X2);
  and and_5 (and_5_out, nand_3_out, not_2_out);
  or or_2 (or_2_out, and_4_out, and_3_out);
  or or_3 (B, or_2_out, and_5_out);
endmodule
