// Digital circuit Solitaire_2c.dig as structural Verilog
module Solitaire_2c (
  input  clk,
  input  A,
  input  B,
  input  C,
  input  X,
  output DC,
  output DB,
  output DA
);

  wire and_1_out, and_2_out, and_3_out, and_4_out, not_1_out, not_2_out, not_3_out, or_1_out, or_2_out;

  not not_1 (not_1_out, B);
  and and_1 (and_1_out, not_1_out, A);
  not not_2 (not_2_out, C);
  and and_2 (and_2_out, C, not_1_out);
  D_FF u_DC (.D(X), .C(clk), .Q(DC));  // open: nQ
  not not_3 (not_3_out, X);
  and and_3 (and_3_out, not_3_out, and_1_out);
  and and_4 (and_4_out, B, not_2_out);
  or or_1 (or_1_out, not_2_out, and_3_out);
  D_FF u_DB (.D(or_1_out), .C(clk), .Q(DB));  // open: nQ
  or or_2 (or_2_out, and_4_out, and_2_out);
  D_FF u_DA (.D(or_2_out), .C(clk), .Q(DA));  // open: nQ
endmodule
