// Digital circuit class_xnot.dig as structural Verilog
module class_xnot (
  input  x,
  input  y,
  input  z,
  output s
);

  wire and_1_out;

  and and_1 (and_1_out, x, y);
  // XOr xor_1 has open pins: In_1=x, In_2=y, out=open
  xor xor_2 (s, and_1_out, z);
  // And and_2 has open pins: In_1=and_1_out, In_2=open, out=open
  // Or or_1 is placed but not wired
endmodule
