// Digital circuit decoder_class.dig as structural Verilog
module decoder_class (
  input  e,
  input  a2,
  input  a1,
  input  a0,
  output d0,
  output d1
);

  wire not_1_out, not_2_out, not_3_out;

  not not_1 (not_1_out, a2);
  not not_2 (not_2_out, a1);
  not not_3 (not_3_out, a0);
  and and_1 (d0, not_3_out, not_2_out, not_1_out, e);
  and and_2 (d1, a0, not_2_out, not_1_out, e);
endmodule
