// Digital circuit multiplexior_class.dig as structural Verilog
module multiplexior_class (
  input  i1,
  input  i2,
  input  i0,
  input  i3,
  input  s0,
  input  s1,
  output out_7
);

  wire and_1_out, and_2_out, and_3_out, and_4_out, not_1_out;

  not not_1 (not_1_out, s0);
  not not_2 (not_1_out, s1);
  and and_1 (and_1_out, i0, not_1_out, not_1_out);
  and and_2 (and_2_out, i1, not_1_out, s1);
  and and_3 (and_3_out, i2, s0, not_1_out);
  and and_4 (and_4_out, i3, s0, s1);
  or or_1 (out_7, and_1_out, and_2_out, and_3_out, and_4_out);
endmodule
